# Fritzing sketch UAS (saved by Fritzing 0.8.7b)
breadboards: 1

parts:
  U1 = NodeMCU V1.0
  Part1 = KY-015 Temperature & Humidity Sensor Module [package="Breakout board"]
  Mod1 = KY-018 Photoresistor Module [package="Breakout board"]

nets:
  N1: U1.D1, Mod1.S
  N2: U1.D2, Part1.Vin
  N3: U1.3V3, Part1.S, Mod1.-
  GND: U1.GND, Part1.-, Mod1.Vin

notes:
  LDR
  DHT11
  Fidela Trisaktiyani
  1841720211

custom parts:
  NodeMCU V1.0: ESP8266 based NodeMCU
  KY-015 Temperature & Humidity Sensor Module: KY-015 temperature and humidity sensor module, provides a low-latency serial interface to measure humidity and temperature.
  KY-018 Photoresistor Module: KY-018 Photoresistor module, used to measure light intensity. It can determine the presence or absence of light.
